# Fritzing sketch Arduino Micro (USB Joystick) 1 Player + Rotary + 15 Pin (Neo Geo) REV.0 (saved by Fritzing 0.9.5d)
circuit board: 6.2cm x 4.1cm
breadboards: 1

parts:
  X1 = DB15 Connector [package=db15]
  Part1 = Arduino Micro (Rev3)
  J1 = screw terminal, 13 pins
  J2 = screw terminal, 10 pins

nets:
  N1: X1.1, Part1.5V, J1.pin1, J2.pin8
  N2: X1.2, Part1.A2, J2.pin4
  N3: X1.3, Part1.A1, J2.pin3
  N4: X1.4, Part1.D5_PWM, J1.pin6
  N5: X1.5, Part1.D7, J1.pin8
  N6: X1.6, Part1.D11_PWM, J1.pin12
  N7: X1.7, Part1.D9_PWM/A9, J1.pin10
  N8: X1.8, Part1.GND, J1.pin2, J2.pin9
  N9: X1.9, Part1.A0, J2.pin2
  N10: X1.10, Part1.A3, J2.pin5
  N11: X1.11, Part1.D4_PWM/A6, J1.pin5
  N12: X1.12, Part1.D6_PWM/A7, J1.pin7
  N13: X1.13, Part1.D12_PWM/A11, J1.pin13
  N14: X1.14, Part1.D8_PWM/A8, J1.pin9
  N15: Part1.D2/SDA, J1.pin3
  N16: Part1.D3/SCL, J1.pin4
  N17: Part1.D10_PWM/A10, J1.pin11
  N18: Part1.MISO, J2.pin10
  N19: Part1.A5, J2.pin7
  N20: Part1.A4, J2.pin6
  N21: Part1.D13_PWM, J2.pin1

custom parts:
  DB15 Connector: DB15 Connector Standard DB15 (D-Sub 15) pc midi or gameport connector. Can be used for old PC compatible joystic.
