# Fritzing sketch Arduino Micro (USB Joystick) 1 Player + Rotary + 15 Pin (Neo Geo) REV.1 (saved by Fritzing 0.9.5d)
circuit board: 7.19cm x 4.1cm
breadboards: 1

parts:
  db15 = DB15 Connector [package=db15]
  Arduino_Micro = Arduino Micro (Rev3)
  J1 = screw terminal, 13 pins
  J2 = screw terminal, 10 pins

nets:
  N1: db15.1, Arduino_Micro.5V, J1.pin1, J2.pin8
  N2: db15.2, Arduino_Micro.A2, J2.pin4
  N3: db15.3, Arduino_Micro.A1, J2.pin3
  N4: db15.4, Arduino_Micro.D5_PWM, J1.pin6
  N5: db15.5, Arduino_Micro.D7, J1.pin8
  N6: db15.6, Arduino_Micro.D11_PWM, J1.pin12
  N7: db15.7, Arduino_Micro.D9_PWM/A9, J1.pin10
  N8: db15.8, Arduino_Micro.GND, J1.pin2, J2.pin9
  N9: db15.9, Arduino_Micro.A0, J2.pin2
  N10: db15.10, Arduino_Micro.A3, J2.pin5
  N11: db15.11, Arduino_Micro.D4_PWM/A6, J1.pin5
  N12: db15.12, Arduino_Micro.D6_PWM/A7, J1.pin7
  N13: db15.13, Arduino_Micro.D12_PWM/A11, J1.pin13
  N14: db15.14, Arduino_Micro.D8_PWM/A8, J1.pin9
  N15: db15.15, Arduino_Micro.D10_PWM/A10, J1.pin11
  N16: Arduino_Micro.D2/SDA, J1.pin3
  N17: Arduino_Micro.D3/SCL, J1.pin4
  N18: Arduino_Micro.MISO, J2.pin10
  N19: Arduino_Micro.A5, J2.pin7
  N20: Arduino_Micro.A4, J2.pin6
  N21: Arduino_Micro.D13_PWM, J2.pin1

notes:
  USB
  B9
  5v
  GND
  OPA
  OPB
  B1
  QT
  Up
  Ri
  Do
  Le
  SFT
  KYB
  B8
  B10
  ATMega32U4
  Neo Geo Input
  B2
  B3
  B4
  B5
  B6
  B7

custom parts:
  DB15 Connector: DB15 Connector Standard DB15 (D-Sub 15) pc midi or gameport connector. Can be used for old PC compatible joystic.
