# Fritzing sketch Arduino Micro - 10 Button USB Joystick with Rotary Encoder (Smaller) REV .1.6 (saved by Fritzing 0.9.5d)
circuit board: 8.57cm x 3.6cm
breadboards: 1

parts:
  Arduino_Micro = Arduino Micro (Rev3)
  DR9_M = DB9 Connector [package=db9]
  5_08mm_7_Pin_Screw_Terminal1_CTB0158/7 = Camdenboss CTB0158-7 [part_number=CTB0158-7 package=THT]
  5_08mm_7_Pin_Screw_Terminal1_CTB0158/7_2 = Camdenboss CTB0158-7 [part_number=CTB0158-7 package=THT]
  5_08mm_6_Pin_Screw_Terminal2_CTB0158/6 = Camdenboss CTB0158-6 [part_number=CTB0158-6 package=THT]

nets:
  N1: Arduino_Micro.GND, DR9_M.8, 5_08mm_7_Pin_Screw_Terminal1_CTB0158/7.pin4
  N2: Arduino_Micro.D2/SDA, 5_08mm_7_Pin_Screw_Terminal1_CTB0158/7.pin5
  N3: Arduino_Micro.D3/SCL, 5_08mm_7_Pin_Screw_Terminal1_CTB0158/7.pin6
  N4: Arduino_Micro.D4_PWM/A6, DR9_M.9, 5_08mm_7_Pin_Screw_Terminal1_CTB0158/7.pin7
  N5: Arduino_Micro.D5_PWM, DR9_M.6, 5_08mm_7_Pin_Screw_Terminal1_CTB0158/7.pin1
  N6: Arduino_Micro.D6_PWM/A7, 5_08mm_7_Pin_Screw_Terminal1_CTB0158/7.pin2
  N7: Arduino_Micro.D7, 5_08mm_6_Pin_Screw_Terminal2_CTB0158/6.pin6
  N8: Arduino_Micro.D8_PWM/A8, 5_08mm_6_Pin_Screw_Terminal2_CTB0158/6.pin5
  N9: Arduino_Micro.D9_PWM/A9, 5_08mm_6_Pin_Screw_Terminal2_CTB0158/6.pin4
  N10: Arduino_Micro.D10_PWM/A10, 5_08mm_6_Pin_Screw_Terminal2_CTB0158/6.pin1
  N11: Arduino_Micro.D11_PWM, 5_08mm_6_Pin_Screw_Terminal2_CTB0158/6.pin2
  N12: Arduino_Micro.D12_PWM/A11, 5_08mm_6_Pin_Screw_Terminal2_CTB0158/6.pin3
  N13: Arduino_Micro.5V, DR9_M.5, 5_08mm_7_Pin_Screw_Terminal1_CTB0158/7.pin3
  N14: Arduino_Micro.A5, 5_08mm_7_Pin_Screw_Terminal1_CTB0158/7_2.pin7
  N15: Arduino_Micro.A4, 5_08mm_7_Pin_Screw_Terminal1_CTB0158/7_2.pin6
  N16: Arduino_Micro.A3, DR9_M.3, 5_08mm_7_Pin_Screw_Terminal1_CTB0158/7_2.pin5
  N17: Arduino_Micro.A2, 5_08mm_7_Pin_Screw_Terminal1_CTB0158/7_2.pin4
  N18: Arduino_Micro.A1, DR9_M.2, DR9_M.4, 5_08mm_7_Pin_Screw_Terminal1_CTB0158/7_2.pin3
  N19: Arduino_Micro.A0, DR9_M.1, 5_08mm_7_Pin_Screw_Terminal1_CTB0158/7_2.pin2
  N20: Arduino_Micro.D13_PWM, 5_08mm_7_Pin_Screw_Terminal1_CTB0158/7_2.pin1

notes:
  USB
  B1
  5v
  OPB
  OPA
  GND
  B2
  B3
  B4
  B5
  B6
  B7
  B8
  B9
  B10
  ATmega32U4
  Down
  Left
  Right
  Up
  [KYB]
  [SHF]
  Amiga 2 Button
