# Fritzing sketch K350 74HC165 Rev.1 (saved by Fritzing 0.9.5d)
circuit board: 9.14cm x 3.69622cm
breadboards: 1

parts:
  Arduino_Micro = Arduino Micro (Rev3)
  74HC165_(A) = 74HC165 [package="DIP16 [THT]"]
  74HC165_(B) = 74HC165 [package="DIP16 [THT]"]
  8_Pin_3_5mm_KA350_Screw_Terminal_(B) = screw terminal, 8 pins
  8_Pin_3_5mm_KA350_Screw_Terminal_(A) = screw terminal, 8 pins
  R1 = Resistor [tolerance=±5% resistance=10k package="0805 [SMD]"]
  R2 = Resistor [tolerance=±5% resistance=10k package="0805 [SMD]"]
  R3 = Resistor [tolerance=±5% resistance=10k package="0805 [SMD]"]
  R4 = Resistor [tolerance=±5% resistance=10k package="0805 [SMD]"]
  R5 = Resistor [tolerance=±5% resistance=10k package="0805 [SMD]"]
  R6 = Resistor [tolerance=±5% resistance=10k package="0805 [SMD]"]
  R7 = Resistor [tolerance=±5% resistance=10k package="0805 [SMD]"]
  R8 = Resistor [tolerance=±5% resistance=10k package="0805 [SMD]"]
  R9 = Resistor [tolerance=±5% resistance=10k package="0805 [SMD]"]
  R10 = Resistor [tolerance=±5% resistance=10k package="0805 [SMD]"]
  R11 = Resistor [tolerance=±5% resistance=10k package="0805 [SMD]"]
  R12 = Resistor [tolerance=±5% resistance=10k package="0805 [SMD]"]
  R13 = Resistor [tolerance=±5% resistance=10k package="0805 [SMD]"]
  R14 = Resistor [tolerance=±5% resistance=10k package="0805 [SMD]"]
  R15 = Resistor [tolerance=±5% resistance=10k package="0805 [SMD]"]
  R16 = Resistor [tolerance=±5% resistance=10k package="0805 [SMD]"]
  12_Pin_3_5mm_KA350_Screw_Terminal_(A) = screw terminal, 12 pins
  12_Pin_3_5mm_KA350_Screw_Terminal_(B) = screw terminal, 12 pins

nets:
  N1: Arduino_Micro.RXLED/SS, 74HC165_(A).Qh
  GND: Arduino_Micro.GND, 74HC165_(A).GND, 74HC165_(A).CLK_Enable, 74HC165_(B).GND, 74HC165_(B).CLK_Enable, 12_Pin_3_5mm_KA350_Screw_Terminal_(A).pin2, 12_Pin_3_5mm_KA350_Screw_Terminal_(B).pin8
  N2: Arduino_Micro.D2/SDA, 12_Pin_3_5mm_KA350_Screw_Terminal_(A).pin3
  N3: Arduino_Micro.D3/SCL, 12_Pin_3_5mm_KA350_Screw_Terminal_(A).pin4
  N4: Arduino_Micro.D4_PWM/A6, 12_Pin_3_5mm_KA350_Screw_Terminal_(A).pin5
  N5: Arduino_Micro.D5_PWM, 12_Pin_3_5mm_KA350_Screw_Terminal_(A).pin6
  N6: Arduino_Micro.D6_PWM/A7, 12_Pin_3_5mm_KA350_Screw_Terminal_(A).pin7
  N7: Arduino_Micro.D7, 12_Pin_3_5mm_KA350_Screw_Terminal_(A).pin8
  N8: Arduino_Micro.D8_PWM/A8, 12_Pin_3_5mm_KA350_Screw_Terminal_(A).pin9
  N9: Arduino_Micro.D9_PWM/A9, 12_Pin_3_5mm_KA350_Screw_Terminal_(A).pin10
  N10: Arduino_Micro.D10_PWM/A10, 12_Pin_3_5mm_KA350_Screw_Terminal_(A).pin11
  N11: Arduino_Micro.D11_PWM, 12_Pin_3_5mm_KA350_Screw_Terminal_(A).pin12
  N12: Arduino_Micro.D12_PWM/A11, 12_Pin_3_5mm_KA350_Screw_Terminal_(B).pin1
  N13: Arduino_Micro.SCK, 12_Pin_3_5mm_KA350_Screw_Terminal_(B).pin12
  N14: Arduino_Micro.MISO, 12_Pin_3_5mm_KA350_Screw_Terminal_(B).pin11
  N15: Arduino_Micro.VIN, 12_Pin_3_5mm_KA350_Screw_Terminal_(B).pin10
  N16: Arduino_Micro.RESET, 12_Pin_3_5mm_KA350_Screw_Terminal_(B).pin9
  VCC: Arduino_Micro.5V, 74HC165_(A).VCC, 74HC165_(B).VCC, R1.Pin_1, R2.Pin_1, R3.Pin_1, R4.Pin_1, R5.Pin_1, R6.Pin_1, R7.Pin_1, R8.Pin_1, R9.Pin_0, R10.Pin_0, R11.Pin_0, R12.Pin_0, R13.Pin_0, R14.Pin_0, R15.Pin_0, R16.Pin_0, 12_Pin_3_5mm_KA350_Screw_Terminal_(A).pin1, 12_Pin_3_5mm_KA350_Screw_Terminal_(B).pin7
  N17: Arduino_Micro.A5, 74HC165_(A).CLK, 74HC165_(B).CLK
  N18: Arduino_Micro.A4, 74HC165_(A).SH/LD', 74HC165_(B).SH/LD'
  N19: Arduino_Micro.A3, 12_Pin_3_5mm_KA350_Screw_Terminal_(B).pin6
  N20: Arduino_Micro.A2, 12_Pin_3_5mm_KA350_Screw_Terminal_(B).pin5
  N21: Arduino_Micro.A1, 12_Pin_3_5mm_KA350_Screw_Terminal_(B).pin4
  N22: Arduino_Micro.A0, 12_Pin_3_5mm_KA350_Screw_Terminal_(B).pin3
  N23: Arduino_Micro.D13_PWM, 12_Pin_3_5mm_KA350_Screw_Terminal_(B).pin2
  N24: 74HC165_(A).E, 8_Pin_3_5mm_KA350_Screw_Terminal_(A).pin5, R12.Pin_1
  N25: 74HC165_(A).F, 8_Pin_3_5mm_KA350_Screw_Terminal_(A).pin6, R11.Pin_1
  N26: 74HC165_(A).G, 8_Pin_3_5mm_KA350_Screw_Terminal_(A).pin7, R10.Pin_1
  N27: 74HC165_(A).H, 8_Pin_3_5mm_KA350_Screw_Terminal_(A).pin8, R9.Pin_1
  N28: 74HC165_(A).SER_Data, 74HC165_(B).Qh
  N29: 74HC165_(A).A, 8_Pin_3_5mm_KA350_Screw_Terminal_(B).pin1, R1.Pin_0
  N30: 74HC165_(A).B, 8_Pin_3_5mm_KA350_Screw_Terminal_(B).pin2, R2.Pin_0
  N31: 74HC165_(A).C, 8_Pin_3_5mm_KA350_Screw_Terminal_(B).pin3, R3.Pin_0
  N32: 74HC165_(A).D, 8_Pin_3_5mm_KA350_Screw_Terminal_(B).pin4, R4.Pin_0
  N33: 74HC165_(B).E, 8_Pin_3_5mm_KA350_Screw_Terminal_(A).pin1, R16.Pin_1
  N34: 74HC165_(B).F, 8_Pin_3_5mm_KA350_Screw_Terminal_(A).pin2, R15.Pin_1
  N35: 74HC165_(B).G, 8_Pin_3_5mm_KA350_Screw_Terminal_(A).pin3, R14.Pin_1
  N36: 74HC165_(B).H, 8_Pin_3_5mm_KA350_Screw_Terminal_(A).pin4, R13.Pin_1
  N37: 74HC165_(B).A, 8_Pin_3_5mm_KA350_Screw_Terminal_(B).pin5, R5.Pin_0
  N38: 74HC165_(B).B, 8_Pin_3_5mm_KA350_Screw_Terminal_(B).pin6, R6.Pin_0
  N39: 74HC165_(B).C, 8_Pin_3_5mm_KA350_Screw_Terminal_(B).pin7, R7.Pin_0
  N40: 74HC165_(B).D, 8_Pin_3_5mm_KA350_Screw_Terminal_(B).pin8, R8.Pin_0

notes:
  USB
  ATMega32U4
  Arcade Controller: 2 Player Joystick, 10 Button & Spinner  - M.Farrell 2020
  P2_B1
  P2_Do
  P2_Le
  P2_B2
  P2_B8
  P2_B9
  5V
  P2_B4
  P2_B3
  P2_B10
  P2_Up
  P2_Ri
  KEYB
  SHFT
  P2_B5
  P2_B7
  P2_B6
  GND
  OPT A
  OPT B
  P1_B1
  P1_B2
  P1_B3
  P1_B4
  P1_B5
  P1_B6
  P1_B7
  P1_B8
  P1_Le
  P1_Ri
  P1_Up
  P1_Do
  P1_B9
  P1_B10
  Reset
  R1-16
  0805
  10K Ω

custom parts:
  74HC165: 8-bit parallel-load shift registers
