# Fritzing sketch Arduino Micro - 10 Button USB Joystick with Rotary Encoder (Smaller - 5.08mm KF301) REV.1.7 (saved by Fritzing 0.9.5d)
circuit board: 8.57cm x 3.6cm
breadboards: 1

parts:
  Arduino_Micro = Arduino Micro (Rev3)
  DR9_M = DB9 Connector [package=db9]
  KF301_7_pin_5_08mm_Terminal = screw terminal, 7 pins
  KF301_13_pin_5_08mm_Terminal = screw terminal, 13 pins

nets:
  N1: Arduino_Micro.GND, DR9_M.8, KF301_7_pin_5_08mm_Terminal.pin4
  N2: Arduino_Micro.D2/SDA, KF301_7_pin_5_08mm_Terminal.pin3
  N3: Arduino_Micro.D3/SCL, KF301_7_pin_5_08mm_Terminal.pin2
  N4: Arduino_Micro.D4_PWM/A6, DR9_M.9, KF301_7_pin_5_08mm_Terminal.pin1
  N5: Arduino_Micro.D5_PWM, DR9_M.6, KF301_7_pin_5_08mm_Terminal.pin7
  N6: Arduino_Micro.D6_PWM/A7, KF301_7_pin_5_08mm_Terminal.pin6
  N7: Arduino_Micro.D7, KF301_13_pin_5_08mm_Terminal.pin1
  N8: Arduino_Micro.D8_PWM/A8, KF301_13_pin_5_08mm_Terminal.pin2
  N9: Arduino_Micro.D9_PWM/A9, KF301_13_pin_5_08mm_Terminal.pin3
  N10: Arduino_Micro.D10_PWM/A10, KF301_13_pin_5_08mm_Terminal.pin6
  N11: Arduino_Micro.D11_PWM, KF301_13_pin_5_08mm_Terminal.pin5
  N12: Arduino_Micro.D12_PWM/A11, KF301_13_pin_5_08mm_Terminal.pin4
  N13: Arduino_Micro.5V, DR9_M.5, KF301_7_pin_5_08mm_Terminal.pin5
  N14: Arduino_Micro.A5, KF301_13_pin_5_08mm_Terminal.pin7
  N15: Arduino_Micro.A4, KF301_13_pin_5_08mm_Terminal.pin8
  N16: Arduino_Micro.A3, DR9_M.3, KF301_13_pin_5_08mm_Terminal.pin9
  N17: Arduino_Micro.A2, KF301_13_pin_5_08mm_Terminal.pin10
  N18: Arduino_Micro.A1, DR9_M.2, DR9_M.4, KF301_13_pin_5_08mm_Terminal.pin11
  N19: Arduino_Micro.A0, DR9_M.1, KF301_13_pin_5_08mm_Terminal.pin12
  N20: Arduino_Micro.D13_PWM, KF301_13_pin_5_08mm_Terminal.pin13

notes:
  USB
  B1
  5v
  OPB
  OPA
  GND
  B2
  B3
  B4
  B5
  B6
  B7
  B8
  B9
  B10
  ATmega32U4
  Down
  Left
  Right
  Up
  [KYB]
  [SHF]
  Amiga 2 Button
